# Fritzing sketch capstone (saved by Fritzing 0.9.3b)
breadboards: 1

parts:
  부품1 = Arduino Nano (Rev3.0) (ICSP)
  J1 = Basic Servo
  M1 = Keyes l9110 Fan module [package=THT]
  A1 = HuskyLens-Vision-Sensor_1

nets:
  GND: 부품1.GND, J1.gnd, M1.pin3, A1.pin3
  N1: 부품1.D2, A1.pin2
  N2: 부품1.D3, A1.pin1
  N3: 부품1.D7, J1.pulse
  N4: 부품1.D11/MOSI, M1.pin2
  N5: 부품1.D12/MISO, M1.pin1
  5V: 부품1.5V, J1.vcc, M1.pin4, A1.pin4

notes:
  캡스톤 디자인

custom parts:
  Keyes l9110 Fan module: Keyes l9110 Fan module. Done from pictures without an actual board to hand so breadboard may not be fully accurate.
  HuskyLens-Vision-Sensor_1: Huskylens is an easy-to-use AI Camera | Vision Sensor. DFrobot Huskylens is equipped with multiple functions, such as face recognition, object tracking, object recognition, line tracking, color recognition, and tag(QR code) recognition.
